# Fritzing sketch Digital Control System Schematic (saved by Fritzing 0.9.10b)

parts:
  U2 = ESP8266 NodeMCU LoLin module
  THERMO1 = MAX31855 Breakout Board with Thermocouple
  OLED_I2C1 = OLED 128x64 I2C Monochrome Display
  IC1 = ULN2803A [package=THT]
  M1 = Stepper Motor - Unipolar

nets:
  N1: U2.D0, THERMO1.CS
  N2: U2.D1, OLED_I2C1.SCK
  N3: U2.D2, OLED_I2C1.SDA
  N4: U2.D3, THERMO1.CLK
  N5: U2.D4, THERMO1.DO
  N6: U2.D5, IC1.In_1
  N7: U2.D6, IC1.In_2
  N8: U2.D7, IC1.In_3
  N9: U2.D8, IC1.In_4
  GND: U2.GND, THERMO1.GND, OLED_I2C1.GND, IC1.0V
  VIN: U2.Vin, OLED_I2C1.VDD
  N10: THERMO1.Vin, IC1.COM_-_Common
  N11: IC1.Out_4, M1.D
  N12: IC1.Out_3, M1.B
  N13: IC1.Out_2, M1.C
  N14: IC1.Out_1, M1.A
  N15: M1.COMMON_1, M1.COMMON_2

notes:
  Unipolar Stepper Motor
  The thermocouple module that was used for the Digital Control System does not have a fritzing file, but it should look similar to this

custom parts:
  ESP8266 NodeMCU LoLin module: ESP8266 based NodeMCU
